# Fritzing sketch Untitled Sketch (saved by Fritzing 0.9.5d)
breadboards: 1

parts:
  M1 = DOIT Esp32 DevKit v1 (30 pins long, 11 pins width) [part_number=ESP32S-PIN30]
  RHT1 = Humidity and Temperature Sensor RHT03
  A1 = Soil Moisture Detection Module
  WATER_PUMP2 = water pump/motor  # not connected
  A2 = 2 channel relay module [package=THT]
  WATER_PUMP3 = water pump/motor  # not connected
  A3 = TANAH pH sensor
  J1 = Basic Servo

nets:
  VCC: M1.3V3, RHT1.Vcc, A1.VCC, A2.pin_13, J1.vcc
  GND: M1.GND, RHT1.GND_2, A1.DO, A1.GND, A2.pin_14, A3.Pin_1, J1.gnd
  N1: M1.D4, RHT1.Data-signal
  N2: M1.D21, J1.pulse
  N3: M1.D34, A3.Pin_2
  N4: M1.D35, A1.AO
  N5: M1.D26, A2.pin_16
  N6: M1.D27, A2.pin_15

custom parts:
  DOIT Esp32 DevKit v1 (30 pins long, 11 pins width): The DOIT Esp32 DevKit v1 is one of the development board created by DOIT to evaluate the ESP-WROOM-32 module. It is based on the ESP32 microcontroller that boasts Wifi, Bluetooth, Ethernet and Low Power support all in a single chip. (vanepp) made breadboard work, adjusted pin numbering and labels and reduced size of schematic and cleaned up pcb. This chip is 30pins long (2 x15) and 11 pins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
  water pump/motor: WATER PUMP BY ARDUBLOCKTR
  2 channel relay module: 2 channel Relay Module 5V 12V 24V High and Low Level Trigger Relay Control With Optocoupler Two Way relays DC 5 V 12 V 24 V Volt.
